# Fritzing sketch Ouch Button Schmatic (saved by Fritzing 0.9.3b)

parts:
  LEDs = IC, SIP package, 4 pins [chip_label=LEDs]
  GPS = IC, SIP package, 4 pins [chip_label=GPS]
  Button = IC, SIP package, 2 pins [chip_label=Button]
  SD_Card = IC, SIP package, 6 pins [chip_label="SD Card"]
  Arduino_Shield = Arduino Prototyping Shield

nets:
  N1: LEDs.pin1, GPS.pin2, Button.pin1, SD_Card.pin6, Arduino_Shield.GND
  N2: LEDs.pin2, Arduino_Shield.D6
  N3: LEDs.pin3, Arduino_Shield.D9
  N4: LEDs.pin4, Arduino_Shield.D10
  N5: GPS.pin1, Arduino_Shield.+5V
  N6: GPS.pin3, Arduino_Shield.D7
  N7: GPS.pin4, Arduino_Shield.D3
  N8: Button.pin2, Arduino_Shield.D5
  N9: SD_Card.pin1, Arduino_Shield.3.3V
  N10: SD_Card.pin2, Arduino_Shield.D4
  N11: SD_Card.pin3, Arduino_Shield.D11
  N12: SD_Card.pin4, Arduino_Shield.D12
  N13: SD_Card.pin5, Arduino_Shield.D13
